# Fritzing sketch projeto_catracas (saved by Fritzing 0.9.3b)
breadboards: 2

parts:
  M1 = DOIT Esp32 DevKit v1 (30 pins long, 11 pins width) [part_number=ESP32S-PIN30]
  S1 = Momentary Switch [package=ksa_sealed_tac_switch]
  S2 = Momentary Switch [package=ksa_sealed_tac_switch]
  LED1 = RGB LED (com. anode, rbg) [package="5 mm [THT]"]
  R2 = Resistor [tolerance=±5% resistance=330 package="2512 [SMD]"]
  R1 = Resistor [tolerance=±5% resistance=10k package="0402 [SMD]"]
  R3 = Resistor [tolerance=±5% resistance=10k package="0402 [SMD]"]
  S3 = Momentary Switch [package=ksa_sealed_tac_switch]
  S4 = Momentary Switch [package=ksa_sealed_tac_switch]
  LED2 = RGB LED (com. anode, rbg) [package="5 mm [THT]"]
  R4 = Resistor [tolerance=±5% resistance=10k package="0402 [SMD]"]
  R5 = Resistor [tolerance=±5% resistance=10k package="0402 [SMD]"]
  R6 = Resistor [tolerance=±5% resistance=330 package="2512 [SMD]"]
  S5 = Momentary Switch [package=ksa_sealed_tac_switch]
  S6 = Momentary Switch [package=ksa_sealed_tac_switch]
  LED3 = RGB LED (com. anode, rbg) [package="5 mm [THT]"]
  R7 = Resistor [tolerance=±5% resistance=10k package="0402 [SMD]"]
  R8 = Resistor [tolerance=±5% resistance=10k package="0402 [SMD]"]
  R9 = Resistor [tolerance=±5% resistance=330 package="2512 [SMD]"]
  S7 = Momentary Switch [package=ksa_sealed_tac_switch]
  S8 = Momentary Switch [package=ksa_sealed_tac_switch]
  LED4 = RGB LED (com. anode, rbg) [package="5 mm [THT]"]
  R10 = Resistor [tolerance=±5% resistance=10k package="0402 [SMD]"]
  R11 = Resistor [tolerance=±5% resistance=10k package="0402 [SMD]"]
  R12 = Resistor [tolerance=±5% resistance=330 package="2512 [SMD]"]
  WeMos_D1_Mini2 = WeMos D1 Mini  # not connected
  S9 = Momentary Switch [package=ksa_sealed_tac_switch]
  R13 = Resistor [tolerance=±5% resistance=10k package="0402 [SMD]"]
  S10 = Momentary Switch [package=ksa_sealed_tac_switch]
  R14 = Resistor [tolerance=±5% resistance=10k package="0402 [SMD]"]
  S11 = Momentary Switch [package=ksa_sealed_tac_switch]
  R15 = Resistor [tolerance=±5% resistance=10k package="0402 [SMD]"]
  S12 = Momentary Switch [package=ksa_sealed_tac_switch]
  R16 = Resistor [tolerance=±5% resistance=10k package="0402 [SMD]"]
  OLED1 = OLED 128x64 I2C Monochrome Display  # not connected
  S13 = Momentary Switch [package=ksa_sealed_tac_switch]  # not connected
  S14 = Momentary Switch [package=ksa_sealed_tac_switch]  # not connected

nets:
  N1: M1.VP, S12.3, S12.4, R16.Pin_1
  N2: M1.VN, S11.3, S11.4, R15.Pin_1
  N3: M1.D34, S10.3, S10.4, R14.Pin_1
  N4: M1.D35, S9.3, S9.4, R13.Pin_1
  N5: S1.2, R1.Pin_0
  N6: S1.4, S2.1, S2.2
  N7: S2.3, S2.4, R3.Pin_0
  N8: LED1.common_anode, R2.Pin_0
  N9: R2.Pin_1, R1.Pin_1, R3.Pin_1, R4.Pin_1, R5.Pin_1, R6.Pin_1, R7.Pin_1, R8.Pin_1, R9.Pin_1, R10.Pin_1, R11.Pin_1, R12.Pin_1
  N10: S3.2, R4.Pin_0
  N11: S3.4, S4.1, S4.2
  N12: S4.3, S4.4, R5.Pin_0
  N13: LED2.common_anode, R6.Pin_0
  N14: S5.2, R7.Pin_0
  N15: S5.4, S6.1, S6.2
  N16: S6.3, S6.4, R8.Pin_0
  N17: LED3.common_anode, R9.Pin_0
  N18: S7.2, R10.Pin_0
  N19: S7.4, S8.1, S8.2
  N20: S8.3, S8.4, R11.Pin_0
  N21: LED4.common_anode, R12.Pin_0
  N22: S9.1, S9.2, S10.1, S10.2, S11.1, S11.2, S12.1, S12.2
  N23: R13.Pin_0, R14.Pin_0, R15.Pin_0, R16.Pin_0

custom parts:
  DOIT Esp32 DevKit v1 (30 pins long, 11 pins width): The DOIT Esp32 DevKit v1 is one of the development board created by DOIT to evaluate the ESP-WROOM-32 module. It is based on the ESP32 microcontroller that boasts Wifi, Bluetooth, Ethernet and Low Power support all in a single chip. (vanepp) made breadboard work, adjusted pin numbering and labels and reduced size of schematic and cleaned up pcb. This chip is 30pins long (2 x15) and 11 pins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
